// Digital circuit ALU_completa_t_Com1_Grupo01.dig as structural Verilog
module ALU_completa_t_Com1_Grupo01 (
  input  [7:0] nro1,
  input  [7:0] nro2,
  input  [2:0] selec,
  output [7:0] resul,
  output [3:0] flags__zcvn
);

  wire comparator_1_eq, not_1_out, not_2_out, not_3_out, not_4_out, not_5_out, notconnected_1_out,
       notconnected_2_out;
  wire [1:1] and_8_out;
  wire [3:0] and_6_out, and_9_out, sumarit_nbits_1_zcvn, xor_2_out;
  wire [3:3] and_2_out, flag_cero_t_com1_grupo01_1_z;
  wire [7:0] and_4_out, and_5_out, and_7_out, funclog_nbits_1_r, sumarit_nbits_1_r, xor_1_out;
  wire [7:7] and_1_out, and_3_out;
  wire [15:0] mul_1_mul;

  not not_1 (not_1_out, selec[2]);
  not not_2 (not_2_out, selec[1]);
  and and_1 (and_1_out[7], selec[1], not_1_out);
  not not_3 (not_3_out, selec[1]);
  and and_2 (and_2_out[3], not_3_out, not_1_out);
  and and_3 (and_3_out[7], selec[2], not_2_out, not_4_out);
  not not_4 (not_4_out, selec[0]);
  SumArit_Nbits sumarit_nbits_1 (.A(nro1), .B(nro2), .OP(selec[0]), .R(sumarit_nbits_1_r), .zcvn(sumarit_nbits_1_zcvn));
  Mul #(.Bits(8)) mul_1 (.a(nro1), .b(nro2), .mul(mul_1_mul));
  FuncLog_Nbits funclog_nbits_1 (.A(nro1), .B(nro2), .OP(selec[0]), .R(funclog_nbits_1_r));
  assign and_4_out = funclog_nbits_1_r & {8{and_1_out[7]}};  // And and_4, 8 bits wide
  assign and_5_out = {8{and_2_out[3]}} & sumarit_nbits_1_r;  // And and_5, 8 bits wide
  assign and_6_out = sumarit_nbits_1_zcvn & {4{and_2_out[3]}};  // And and_6, 4 bits wide
  assign and_7_out = mul_1_mul[7:0] & {8{and_3_out[7]}};  // And and_7, 8 bits wide
  Comparator #(.Bits(8)) comparator_1 (.a(mul_1_mul[15:8]), .b({8{1'b0}}), .eq(comparator_1_eq));  // open: gt, lt
  not not_5 (not_5_out, comparator_1_eq);
  flag_cero_t_Com1_Grupo01 flag_cero_t_com1_grupo01_1 (.S(and_4_out), .Z(flag_cero_t_com1_grupo01_1_z[3]));
  and and_8 (and_8_out[1], not_5_out, and_3_out[7]);
  assign xor_1_out = and_4_out ^ and_5_out;  // XOr xor_1, 8 bits wide
  assign xor_2_out = {2'b00, and_8_out[1], 1'b0} ^ and_6_out;  // XOr xor_2, 4 bits wide
  assign and_9_out = {flag_cero_t_com1_grupo01_1_z[3], 2'b00, and_4_out[7]} & {4{and_1_out[7]}};  // And and_9, 4 bits wide
  assign resul = and_7_out ^ xor_1_out;  // XOr xor_3, 8 bits wide
  Seven_Seg_Hex seven_seg_hex_1 (.d(resul[3:0]), .dp(notconnected_1_out));
  assign flags__zcvn = xor_2_out ^ and_9_out;  // XOr xor_4, 4 bits wide
  Seven_Seg_Hex seven_seg_hex_2 (.d(resul[7:4]), .dp(notconnected_2_out));
  // NotConnected on notconnected_1_out
  // NotConnected on notconnected_2_out
endmodule
