// Digital circuit FuncLog_Nbits.dig as structural Verilog
module FuncLog_Nbits (
  input  [3:0] A,
  input  [3:0] B,
  input  OP,
  output [3:0] R
);

  wire [3:0] and_1_out, and_2_out, and_3_out, not_1_out, or_1_out;

  assign or_1_out = A | B;  // Or or_1, 4 bits wide
  assign and_1_out = B & A;  // And and_1, 4 bits wide
  assign not_1_out = ~{4{OP}};  // Not not_1, 4 bits wide
  assign and_2_out = or_1_out & {4{OP}};  // And and_2, 4 bits wide
  assign and_3_out = and_1_out & not_1_out;  // And and_3, 4 bits wide
  assign R = and_2_out ^ and_3_out;  // XOr xor_1, 4 bits wide
endmodule
