// Digital circuit complementadorA2_t_Com1_Grupo01.dig as structural Verilog
module complementadorA2_t_Com1_Grupo01 (
  input  [7:0] B_2,
  input  Neg,
  output [7:0] B
);

  wire notconnected_1_out, notconnected_2_out;
  wire [7:0] xor_1_out;

  assign xor_1_out = B_2 ^ {8{Neg}};  // XOr xor_1, 8 bits wide
  sum_4bit_t_Com1_Grupo01 sum_4bit_t_com1_grupo01_1 (.A(xor_1_out), .B({8{Neg}}), .Cin(Neg), .S(B));  // open: Cout
  Seven_Seg_Hex seven_seg_hex_1 (.d(B[3:0]), .dp(notconnected_1_out));
  // NotConnected on notconnected_1_out
  Seven_Seg_Hex seven_seg_hex_2 (.d(B[7:4]), .dp(notconnected_2_out));
  // NotConnected on notconnected_2_out
endmodule
