// Digital circuit flag_cero_t_Com1_Grupo01.dig as structural Verilog
module flag_cero_t_Com1_Grupo01 (
  input  [7:0] S,
  output Z
);

  nor nor_1 (Z, S[0], S[1], S[2], S[3], S[4], S[5], S[6], S[7]);
endmodule
