// Digital circuit flag_overflow_t_Com1_Grupo01.dig as structural Verilog
module flag_overflow_t_Com1_Grupo01 (
  input  a3,
  input  b3,
  input  s3,
  output V
);

  wire and_1_out, and_2_out, not_1_out, not_2_out, not_3_out;

  not not_1 (not_1_out, a3);
  not not_2 (not_2_out, b3);
  not not_3 (not_3_out, s3);
  and and_1 (and_1_out, not_1_out, not_2_out, s3);
  and and_2 (and_2_out, a3, b3, not_3_out);
  xor xor_1 (V, and_1_out, and_2_out);
endmodule
